# Fritzing sketch eee428_schematic (saved by Fritzing 0.9.3b)
breadboards: 1

parts:
  LED3 = LED - 3mm [color="Red (633nm)" package="3 mm [THT]"]
  R1 = Resistor [tolerance=±5% resistance=220 package="2010 [SMD]"]
  Grove1 = Grove OLED 128x96
  U1 = GAS_SENSOR [package=mq-3]
  R2 = Resistor [tolerance=±5% resistance=220 package="2010 [SMD]"]
  microSD_Transflash1 = SparkFun - microSD Transflash
  Mod1 = sensor_biometrico
  L1 = Solenoid
  J1 = Piezo Speaker
  Part1 = Arduino Uno (Rev3)

nets:
  N1: LED3.cathode, J1.pin2, Part1.D4
  N2: LED3.anode, R1.Pin_0
  GND: R1.Pin_1, Grove1.GND, U1.A1, R2.Pin_1, microSD_Transflash1.GND, Mod1.GND, L1.pin1, J1.pin1, Part1.GND
  VCC: Grove1.VCC, U1.H2, microSD_Transflash1.VCC, Mod1.VCC, Part1.5V
  N3: Grove1.SDA, Part1.A4/SDA
  N4: Grove1.SCL, Part1.A5/SCL
  N5: U1.B1, R2.Pin_0
  N6: microSD_Transflash1.CD, Part1.D11_PWM/MOSI
  N7: microSD_Transflash1.DO, Part1.D12/MISO
  N8: microSD_Transflash1.SCK, Part1.D13/SCK
  N9: microSD_Transflash1.DI, Part1.D9_PWM
  N10: Mod1.TX, Part1.D2
  N11: Mod1.RX, Part1.D3_PWM
  N12: L1.pin2, Part1.D5_PWM

custom parts:
  sensor_biometrico: Adafruit Optical Fingerprint Sensor
